# Fritzing sketch DropSensorBreadboard (saved by Fritzing 0.8.3b)
breadboards: 1

parts:
  WeMos_D1_Mini1 = WeMos D1 Mini
  Q1 = NPN-Transistor [package="TO92 [THT]"]
  Q2 = NPN-Transistor [package="TO92 [THT]"]
  R1 = Resistor [tolerance=±5% resistance=220 package=THT]
  R2 = Resistor [tolerance=±5% resistance=220 package=THT]
  Q3 = LTR-301 [package=ltr-301]
  R3 = Resistor [tolerance=±5% resistance=1k package=THT]
  LED1 = LED - 5mm [color="Red (633nm)" package="5 mm [THT]"]
  R4 = Resistor [tolerance=±5% resistance=22 package=THT]

nets:
  N1: WeMos_D1_Mini1.3V3, Q3.C, R4.Pin_0
  N2: WeMos_D1_Mini1.A0, Q3.E, R3.Pin_1
  N3: WeMos_D1_Mini1.D1, R1.Pin_0
  N4: WeMos_D1_Mini1.D2, R2.Pin_0
  N5: WeMos_D1_Mini1.G, Q1.E, Q2.E, R3.Pin_0, LED1.cathode
  N6: Q1.B, R1.Pin_1
  N7: Q2.B, R2.Pin_1
  N8: LED1.anode, R4.Pin_1

notes:
  Black -> camera GND
  Orange -> Focus Pin
  Yellow -> Shutter Pin
  IR LED and IR Transistor for breakbeam sensor (Note don't use a RED LED as shown here; I just dont have an IR LED for Fritzing)
